// Logisim project Calculator.circ as structural Verilog: 4 circuits, main circuit main
module main (
  input  [7:0] in_1
);

  wire a, and_1_out, and_2_out, and_3_out, and_4_out, and_5_out, and_7_out, and_8_out, and_9_out, and_10_out,
       and_12_out, and_13_out, and_14_out, and_16_out, and_17_out, and_18_out, b, c, d, e, f, Final_R0,
       Final_R1, Final_R2, Final_R3, Final_Sign, full_adder_1_out_4, full_adder_1_out_5, g,
       half_adder_1_out_3, half_adder_1_out_4, half_adder_2_out_3, half_adder_2_out_4, half_adder_3_out_4,
       half_adder_4_out_4, not_1_out, not_2_out, not_3_out, not_4_out, not_5_out, not_6_out, not_7_out,
       NotZero_B, or_3_out, or_4_out, R0, R0DIV, R0MUP, R1, R1DIV, R1MUP, R2, R2MUP, R3MUP, S_M_D,
       Sign_B_new, Sign_R, xor_2_out, xor_3_out, xor_4_out, xor_5_out, xor_6_out, xor_7_out, xor_8_out,
       xor_9_out, xor_10_out, xor_11_out, Zero_A;

  and and_1 (and_1_out, in_1[1], not_1_out);
  not not_1 (not_1_out, in_1[0]);
  and and_2 (and_2_out, and_1_out, NotZero_B);
  xor xor_1 (Sign_B_new, and_2_out, in_1[6]);
  _7_Segment_Display u_7_segment_display_1 (
    .g(Final_Sign), .f(1'b0), .a(1'b0), .b(1'b0), .e(1'b0), .d(1'b0), .c(1'b0), .dp(1'b0));
  _7_Segment_Display u_7_segment_display_2 (.g(g), .f(f), .a(a), .b(b), .e(e), .d(d), .c(c), .dp(1'b0));
  xor xor_2 (xor_2_out, in_1[7], Sign_B_new);
  and and_3 (and_3_out, in_1[7], xor_2_out);
  and and_4 (and_4_out, xor_2_out, Sign_B_new);
  xor xor_3 (xor_3_out, in_1[5], and_3_out);
  xor xor_4 (xor_4_out, in_1[4], and_3_out);
  xor xor_5 (xor_5_out, and_4_out, in_1[3]);
  xor xor_6 (xor_6_out, and_4_out, in_1[2]);
  Multiplexer #(.select(2)) multiplexer_1 (
    .in0(Sign_R), .in1(Sign_R), .in2(S_M_D), .in3(S_M_D), .out(Final_Sign), .sel({in_1[0], in_1[1]}));  // open: en
  Half_Adder half_adder_1 (.in_1(xor_3_out), .in_2(and_3_out), .out_3(half_adder_1_out_3), .out_4(half_adder_1_out_4));
  Half_Adder half_adder_2 (.in_1(xor_5_out), .in_2(and_4_out), .out_3(half_adder_2_out_3), .out_4(half_adder_2_out_4));
  xor xor_7 (xor_7_out, half_adder_1_out_4, xor_4_out);
  xor xor_8 (xor_8_out, half_adder_2_out_4, xor_6_out);
  Half_Adder half_adder_3 (
    .in_1(half_adder_1_out_3), .in_2(half_adder_2_out_3), .out_3(R0), .out_4(half_adder_3_out_4));
  Multiplexer #(.select(2)) multiplexer_2 (
    .in0(R0), .in1(R0), .in2(R0MUP), .in3(R0DIV), .out(Final_R0), .sel({in_1[0], in_1[1]}));  // open: en
  Full_Adder full_adder_1 (
    .in_1(xor_7_out), .in_2(xor_8_out), .in_3(half_adder_3_out_4), .out_4(full_adder_1_out_4),
    .out_5(full_adder_1_out_5));
  not not_2 (not_2_out, full_adder_1_out_5);
  not not_3 (not_3_out, xor_2_out);
  not not_4 (not_4_out, R0);
  and and_5 (and_5_out, not_2_out, xor_2_out);
  and and_6 (R2, full_adder_1_out_5, not_3_out);
  Multiplexer #(.select(2)) multiplexer_3 (
    .in0(R1), .in1(R1), .in2(R1MUP), .in3(R1DIV), .out(Final_R1), .sel({in_1[0], in_1[1]}));  // open: en
  xor xor_9 (xor_9_out, full_adder_1_out_5, xor_2_out);
  and and_7 (and_7_out, not_4_out, and_5_out);
  xor xor_10 (xor_10_out, and_5_out, full_adder_1_out_4);
  xor xor_11 (xor_11_out, xor_9_out, R2);
  and and_8 (and_8_out, not_3_out, in_1[7]);
  Multiplexer #(.select(2)) multiplexer_4 (
    .in0(R2), .in1(R2), .in2(R2MUP), .in3(1'b0), .out(Final_R2), .sel({in_1[0], in_1[1]}));  // open: en
  ToBcd tobcd_1 (
    .w0(1'b0), .w1(Final_R2), .w2(Final_R1), .w3(Final_R0), .a(a), .b(b), .c(c), .d(d), .e(e), .f(f), .g(g));
  xor xor_12 (R1, and_7_out, xor_10_out);
  or or_1 (Sign_R, xor_11_out, and_8_out);
  Multiplexer #(.select(2)) multiplexer_5 (
    .in0(1'b0), .in1(1'b0), .in2(R3MUP), .in3(1'b0), .out(Final_R3), .sel({in_1[0], in_1[1]}));  // open: en
  not not_5 (not_5_out, in_1[2]);
  and and_9 (and_9_out, in_1[4], NotZero_B);
  or or_2 (NotZero_B, in_1[2], in_1[3]);
  and and_10 (and_10_out, NotZero_B, in_1[5]);
  and and_11 (R0MUP, in_1[5], in_1[3]);
  and and_12 (and_12_out, in_1[5], in_1[2]);
  and and_13 (and_13_out, in_1[3], in_1[4]);
  and and_14 (and_14_out, in_1[2], in_1[4]);
  and and_15 (R1DIV, and_9_out, not_5_out);
  not not_6 (not_6_out, in_1[3]);
  not not_7 (not_7_out, NotZero_B);
  LED led_1 (.in(not_7_out));
  or or_3 (or_3_out, not_7_out, Zero_A);
  LED led_2 (.in(or_3_out));
  Half_Adder half_adder_4 (.in_1(and_12_out), .in_2(and_13_out), .out_3(R1MUP), .out_4(half_adder_4_out_4));
  Half_Adder half_adder_5 (.in_1(half_adder_4_out_4), .in_2(and_14_out), .out_3(R2MUP), .out_4(R3MUP));
  nor nor_1 (Zero_A, in_1[4], in_1[5]);
  and and_16 (and_16_out, and_9_out, not_6_out);
  and and_17 (and_17_out, and_9_out, and_10_out);
  and and_18 (and_18_out, not_5_out, and_10_out);
  LED led_3 (.in(Zero_A));
  or or_4 (or_4_out, and_18_out, and_16_out);
  xor xor_13 (S_M_D, in_1[7], in_1[6]);
  or or_5 (R0DIV, or_4_out, and_17_out);

  // Other names for the same wires on the sheet: B1 = in_1[2]; B0 = in_1[3]; A1 = in_1[4]; A0 = in_1[5];
  //   Sign_B = in_1[6]; Sign_A = in_1[7]; M0 = in_1[1]; Mode[1:0] = {in_1[0], in_1[1]}; M1 = in_1[0]

  // Notes on the sheet:
  //   divid by 0 flag
  //   ZERO FLAG
  //   ZERO FLAG
endmodule

// H A
module Half_Adder (
  input  in_1,
  input  in_2,
  output out_3,
  output out_4
);

  xor xor_1 (out_3, in_1, in_2);
  and and_1 (out_4, in_1, in_2);
endmodule

// F A
module Full_Adder (
  input  in_1,
  input  in_2,
  input  in_3,
  output out_4,
  output out_5
);

  wire half_adder_1_out_3, half_adder_1_out_4, half_adder_2_out_4;

  Half_Adder half_adder_1 (.in_1(in_1), .in_2(in_2), .out_3(half_adder_1_out_3), .out_4(half_adder_1_out_4));
  Half_Adder half_adder_2 (.in_1(half_adder_1_out_3), .in_2(in_3), .out_3(out_4), .out_4(half_adder_2_out_4));
  or or_1 (out_5, half_adder_2_out_4, half_adder_1_out_4);
endmodule

module ToBcd (
  input  w0,
  input  w1,
  input  w2,
  input  w3,
  output a,
  output b,
  output c,
  output d,
  output e,
  output f,
  output g
);

  wire and_1_out, and_2_out, and_3_out, and_4_out, and_5_out, and_6_out, and_7_out, and_8_out, and_9_out,
       and_10_out, and_11_out, and_12_out, and_13_out, and_14_out, and_15_out, and_16_out, and_17_out,
       and_18_out, and_19_out, and_20_out, and_21_out, and_22_out, and_23_out, and_24_out, and_25_out,
       and_26_out, and_27_out, and_28_out, and_29_out, and_30_out, and_31_out, and_32_out, and_33_out,
       and_34_out, and_35_out, not_1_out, not_2_out, not_3_out, not_4_out, not_5_out, not_6_out, not_7_out,
       not_8_out, not_9_out, not_10_out, not_11_out, not_12_out, not_13_out, not_14_out, not_15_out,
       not_16_out, not_17_out, not_18_out, not_19_out, not_20_out, not_21_out, not_22_out, not_23_out,
       not_24_out, not_25_out, not_26_out, not_27_out, not_28_out, not_29_out, not_30_out, not_31_out,
       not_32_out, not_33_out, not_34_out, not_35_out, not_36_out, not_37_out, not_38_out, not_39_out,
       not_40_out, not_41_out, not_42_out, not_43_out;

  not not_1 (not_1_out, w1);
  and and_1 (and_1_out, not_1_out, not_2_out);
  not not_2 (not_2_out, w3);
  not not_3 (not_3_out, w0);
  and and_2 (and_2_out, not_3_out, w2);
  not not_4 (not_4_out, w0);
  and and_3 (and_3_out, not_4_out, w1, w3);
  and and_4 (and_4_out, w1, w2);
  not not_5 (not_5_out, w1);
  and and_5 (and_5_out, w0, not_5_out, not_6_out);
  not not_6 (not_6_out, w2);
  and and_6 (and_6_out, w0, not_7_out);
  not not_7 (not_7_out, w3);
  not not_8 (not_8_out, w0);
  and and_7 (and_7_out, not_8_out, not_9_out);
  not not_9 (not_9_out, w1);
  not not_10 (not_10_out, w0);
  not not_11 (not_11_out, w2);
  and and_8 (and_8_out, not_10_out, not_11_out, not_12_out);
  not not_12 (not_12_out, w3);
  not not_13 (not_13_out, w1);
  and and_9 (and_9_out, not_13_out, not_14_out);
  not not_14 (not_14_out, w3);
  not not_15 (not_15_out, w0);
  and and_10 (and_10_out, not_15_out, w2, w3);
  not not_16 (not_16_out, w2);
  and and_11 (and_11_out, w0, not_16_out, w3);
  not not_17 (not_17_out, w0);
  and and_12 (and_12_out, not_17_out, not_18_out);
  not not_18 (not_18_out, w2);
  not not_19 (not_19_out, w0);
  and and_13 (and_13_out, not_19_out, w3);
  not not_20 (not_20_out, w2);
  and and_14 (and_14_out, not_20_out, w3);
  not not_21 (not_21_out, w0);
  and and_15 (and_15_out, not_21_out, w1);
  and and_16 (and_16_out, w0, not_22_out);
  not not_22 (not_22_out, w1);
  not not_23 (not_23_out, w0);
  not not_24 (not_24_out, w1);
  and and_17 (and_17_out, not_23_out, not_24_out, not_25_out);
  not not_25 (not_25_out, w3);
  not not_26 (not_26_out, w1);
  and and_18 (and_18_out, not_26_out, w2, w3);
  not not_27 (not_27_out, w2);
  and and_19 (and_19_out, w1, not_27_out, w3);
  and and_20 (and_20_out, w1, w2, not_28_out);
  not not_28 (not_28_out, w3);
  and and_21 (and_21_out, w0, not_29_out);
  not not_29 (not_29_out, w2);
  not not_30 (not_30_out, w1);
  and and_22 (and_22_out, not_30_out, not_31_out);
  not not_31 (not_31_out, w3);
  and and_23 (and_23_out, w2, not_32_out);
  not not_32 (not_32_out, w3);
  and and_24 (and_24_out, w0, w2);
  and and_25 (and_25_out, w0, w1);
  not not_33 (not_33_out, w2);
  and and_26 (and_26_out, not_33_out, not_34_out);
  not not_34 (not_34_out, w3);
  not not_35 (not_35_out, w0);
  and and_27 (and_27_out, not_35_out, w1, not_36_out);
  not not_36 (not_36_out, w2);
  and and_28 (and_28_out, w1, not_37_out);
  not not_37 (not_37_out, w3);
  and and_29 (and_29_out, w0, not_38_out);
  not not_38 (not_38_out, w1);
  and and_30 (and_30_out, w0, w2);
  not not_39 (not_39_out, w1);
  and and_31 (and_31_out, not_39_out, w2);
  and and_32 (and_32_out, w2, not_40_out);
  not not_40 (not_40_out, w3);
  not not_41 (not_41_out, w0);
  and and_33 (and_33_out, not_41_out, w1, not_42_out);
  not not_42 (not_42_out, w2);
  and and_34 (and_34_out, w0, not_43_out);
  not not_43 (not_43_out, w1);
  and and_35 (and_35_out, w0, w3);
  or or_1 (b, and_7_out, and_8_out, and_9_out, and_10_out, and_11_out);
  or or_2 (c, and_12_out, and_13_out, and_14_out, and_15_out, and_16_out);
  or or_3 (d, and_17_out, and_18_out, and_19_out, and_20_out, and_21_out);
  or or_4 (e, and_22_out, and_23_out, and_24_out, and_25_out);
  or or_5 (f, and_26_out, and_27_out, and_28_out, and_29_out, and_30_out);
  or or_6 (g, and_31_out, and_32_out, and_33_out, and_34_out, and_35_out);
  or or_7 (a, and_1_out, and_2_out, and_3_out, and_4_out, and_5_out, and_6_out);
endmodule
